# Fritzing sketch joystick_wiring (saved by Fritzing 0.9.3b)
breadboards: 1

parts:
  Raspberry_Pi_1 = Raspberry Pi 3 [part_number=RPI-3-V1.2]  # not connected
  Part2 = Adafruit Pi Cobbler Plus [part_number="Adafruit #2029"]
  IC1 = MCP3008 8-channel 10-bit ADC [part_number=MCP3008]  # not connected
  IC2 = MCP3008 8-channel 10-bit ADC [part_number=MCP3008]  # not connected
  IC3 = MCP3008 8-channel 10-bit ADC [part_number=MCP3008]
  Part3 = Parallax 2-Axis Joystick  # not connected
  J1 = Basic Servo  # not connected

nets:
  N1: Part2.+3.3V, IC3.no_name_yet#16
  N2: IC3.no_name_yet#9, IC3.no_name_yet#14

custom parts:
  Adafruit Pi Cobbler Plus: The Raspberry Pi B+/Pi 2/ Pi 3 has landed on the Maker World like a 40-GPIO pinned, quad-USB ported, credit card sized bomb of DIY joy. And while you can use most of our great Model B accessories by hooking up our downgrade cable, its probably a good time to upgrade your set up and accessorize using all of the Model B+'s / Pi 2's / Pi 3's 40 pins. That's why we now carry the Adafruit Assembled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
  Parallax 2-Axis Joystick: Description: This is the Parallax 2-Axis Joystick. It contains a spring return thumb joystick mounted to a breakout board. The breakout board breaks out the joysticks connections to .1" pin headers. The joystick's connections are duplicated on both sides of the board for easy use. This part can easily be used on a breadboard due to the .1" pin headers, but can also be soldered into any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
